# Fritzing sketch diagrama_ejercicio_1 (saved by Fritzing 0.9.3b)
breadboards: 1

parts:
  Arduino = Arduino Uno (Rev3)
  RFID-RC522 = RFID-RC522-v2

nets (from the schematic view):
  N1: Arduino.D9_PWM, RFID-RC522.GND
  N2: Arduino.D10_PWM/SS, RFID-RC522.SDA
  N3: Arduino.D11_PWM/MOSI, RFID-RC522.MOSI
  N4: Arduino.D12/MISO, RFID-RC522.MISO
  N5: Arduino.D13/SCK, RFID-RC522.SCK
  N6: Arduino.GND, RFID-RC522.RST
  3V3: Arduino.3V3, RFID-RC522.3.3V

custom parts:
  RFID-RC522-v2: A simple China made RFID-RC522 Reader; do check the pin labels, as this is a MFRC522 based clone.
