# Fritzing sketch diagrama_ejercicio_2 (saved by Fritzing 0.9.3b)
breadboards: 1

parts:
  Arduino = Arduino Uno (Rev3)
  RFID-RC522 = RFID-RC522-v2
  R1 = Resistor [tolerance=±5% resistance=220 package="0805 [SMD]"]
  LED1 = smd LED [color="Green (555nm)" package="0805 [SMD]"]

nets:
  GND: Arduino.D9_PWM, Arduino.GND, RFID-RC522.GND, RFID-RC522.RST, R1.Pin_0
  N1: Arduino.D10_PWM/SS, RFID-RC522.SDA
  N2: Arduino.D11_PWM/MOSI, RFID-RC522.MOSI
  N3: Arduino.D12/MISO, RFID-RC522.MISO
  N4: Arduino.D13/SCK, RFID-RC522.SCK
  N5: Arduino.D2, LED1.anode
  3V3: Arduino.3V3, RFID-RC522.3.3V
  N6: R1.Pin_1, LED1.cathode

custom parts:
  RFID-RC522-v2: A simple China made RFID-RC522 Reader; do check the pin labels, as this is a MFRC522 based clone.
